# Fritzing sketch PiBot (saved by Fritzing 0.9.3b)

parts:
  MCU1 = Raspberry Pi Zero
  HC-SR04_Sensor_1 = HC-SR04 Ultrasonic Distance Sensor
  M1 = DC Motor
  S1 = H-Bridge with L298N
  MOTOR1 = 28BYJ-48 Stepper Motor
  BREAKOUT1 = ULN2003A breakout board
  VCC1 = 4 x AAA Battery Mount
  M2 = DC Motor
  R2 = Resistor [tolerance=±5% resistance=470 package="0805 [SMD]"]
  R1 = Resistor [tolerance=±5% resistance=330 package="1206 [SMD]"]

nets:
  VCC: MCU1.pin_2, MCU1.pin_4, HC-SR04_Sensor_1.VCC, BREAKOUT1.+5V
  GND: MCU1.pin_6, MCU1.pin_9, MCU1.pin_34, MCU1.pin_39, HC-SR04_Sensor_1.GND, S1.GND, BREAKOUT1.0V, VCC1.-, R2.Pin_0
  N1: MCU1.pin_7, R2.Pin_1, R1.Pin_0
  N2: MCU1.pin_11, HC-SR04_Sensor_1.TRIG
  N3: MCU1.pin_23, S1.ENB
  N4: MCU1.pin_29, S1.IN4
  N5: MCU1.pin_31, S1.IN3
  N6: MCU1.pin_32, BREAKOUT1.In_4
  N7: MCU1.pin_33, S1.IN2
  N8: MCU1.pin_35, S1.IN1
  N9: MCU1.pin_36, BREAKOUT1.In_3
  N10: MCU1.pin_37, S1.ENA
  N11: MCU1.pin_38, BREAKOUT1.In_2
  N12: MCU1.pin_40, BREAKOUT1.In_1
  N13: HC-SR04_Sensor_1.ECHO, R1.Pin_1
  N14: M1.pin_1, S1.M2-02
  N15: M1.pin_2, S1.M2-01
  N16: S1.12V, VCC1.+
  N17: S1.M1-01, M2.pin_2
  N18: S1.M1-02, M2.pin_1
  N19: MOTOR1.BLUE, BREAKOUT1.BLUE_wire
  N20: MOTOR1.PINK, BREAKOUT1.PINK_wire
  N21: MOTOR1.RED, BREAKOUT1.YELLOW_wire
  N22: MOTOR1.ORANGE, BREAKOUT1.ORANGE_wire
  N23: MOTOR1.YELLOW, BREAKOUT1.RED_wire

custom parts:
  H-Bridge with L298N: h-bridge
  28BYJ-48 Stepper Motor: 28BYJ-48 gear-reduction stepper motor (small)
  ULN2003A breakout board: ULN2003A 7-way Darlington Transistor Driver on breakoutboard
